# Fritzing sketch circuit (saved by Fritzing 0.9.3b)
breadboards: 1

parts:
  LED1 = LED - 5mm [color="Red (633nm)" package="5 mm [THT]"]
  LED2 = LED - 5mm [color="Red (633nm)" package="5 mm [THT]"]
  LED3 = LED - 5mm [color="Red (633nm)" package="5 mm [THT]"]
  LED4 = LED - 5mm [color="Red (633nm)" package="5 mm [THT]"]
  LED5 = LED - 5mm [color="Red (633nm)" package="5 mm [THT]"]
  LED6 = LED - 5mm [color="Red (633nm)" package="5 mm [THT]"]
  LED7 = LED - 5mm [color="Red (633nm)" package="5 mm [THT]"]
  LED8 = LED - 5mm [color="Red (633nm)" package="5 mm [THT]"]
  LED10 = LED - 5mm [color="Red (633nm)" package="5 mm [THT]"]
  LED11 = LED - 5mm [color="Red (633nm)" package="5 mm [THT]"]
  R3 = Resistor [tolerance=±5% resistance=56 package=THT]
  R4 = Resistor [tolerance=±5% resistance=56 package=THT]
  R5 = Resistor [tolerance=±5% resistance=56 package=THT]
  R6 = Resistor [tolerance=±5% resistance=56 package=THT]
  R7 = Resistor [tolerance=±5% resistance=56 package=THT]
  R8 = Resistor [tolerance=±5% resistance=56 package=THT]
  R9 = Resistor [tolerance=±5% resistance=56 package=THT]
  R10 = Resistor [tolerance=±5% resistance=56 package=THT]
  R11 = Resistor [tolerance=±5% resistance=56 package=THT]
  R12 = Resistor [tolerance=±5% resistance=56 package=THT]
  Raspberry_Pi_1 = Raspberry Pi 3 [part_number=RPI-3-V1.2]

nets:
  N1: LED1.cathode, R12.Pin_1
  N2: LED1.anode, Raspberry_Pi_1.GIPO17
  N3: LED2.cathode, R11.Pin_1
  N4: LED2.anode, Raspberry_Pi_1.GIPO18
  N5: LED3.cathode, R3.Pin_1
  N6: LED3.anode, Raspberry_Pi_1.GIPO22
  N7: LED4.cathode, R4.Pin_1
  N8: LED4.anode, Raspberry_Pi_1.GIPO27
  N9: LED5.cathode, R7.Pin_1
  N10: LED5.anode, Raspberry_Pi_1.GIPO25
  N11: LED6.cathode, R6.Pin_1
  N12: LED6.anode, Raspberry_Pi_1.GIPO23
  N13: LED7.cathode, R5.Pin_1
  N14: LED7.anode, Raspberry_Pi_1.GIPO24
  N15: LED8.cathode, R8.Pin_1
  N16: LED8.anode, Raspberry_Pi_1.GIPO10
  N17: LED10.cathode, R10.Pin_1
  N18: LED10.anode, Raspberry_Pi_1.GIPO9
  N19: LED11.cathode, R9.Pin_1
  N20: LED11.anode, Raspberry_Pi_1.GIPO11
  N21: R3.Pin_0, R4.Pin_0, R5.Pin_0, R6.Pin_0, R7.Pin_0, R8.Pin_0, R9.Pin_0, R10.Pin_0, R11.Pin_0, R12.Pin_0, Raspberry_Pi_1.GND
