# Fritzing sketch astro_space_1 (saved by Fritzing 1.0.2b)
breadboards: 1

parts:
  Mod1 = Raspberry Pi 4B
  LED10 = smd LED [color="Red (633nm)" package="0805 [SMD]"]
  R10 = Resistor [tolerance=±5% resistance=47 package="0402 [SMD]"]

nets:
  N1: Mod1.GND, LED10.cathode
  N2: Mod1.GPIO14, R10.Pin_1
  N3: LED10.anode, R10.Pin_0
