# Fritzing sketch astro_space_10 (saved by Fritzing 1.0.2b)
breadboards: 1

parts:
  Mod1 = Raspberry Pi 4B
  LED1 = smd LED [color="Red (633nm)" package="0805 [SMD]"]
  R1 = Resistor [tolerance=±5% resistance=47 package="0402 [SMD]"]
  LED2 = smd LED [color="Red (633nm)" package="0805 [SMD]"]
  LED3 = smd LED [color="Red (633nm)" package="0805 [SMD]"]
  LED4 = smd LED [color="Red (633nm)" package="0805 [SMD]"]
  LED5 = smd LED [color="Red (633nm)" package="0805 [SMD]"]
  LED6 = smd LED [color="Red (633nm)" package="0805 [SMD]"]
  LED7 = smd LED [color="Red (633nm)" package="0805 [SMD]"]
  LED8 = smd LED [color="Red (633nm)" package="0805 [SMD]"]
  LED9 = smd LED [color="Red (633nm)" package="0805 [SMD]"]
  LED10 = smd LED [color="Red (633nm)" package="0805 [SMD]"]
  R2 = Resistor [tolerance=±5% resistance=47 package="0402 [SMD]"]
  R3 = Resistor [tolerance=±5% resistance=47 package="0402 [SMD]"]
  R4 = Resistor [tolerance=±5% resistance=47 package="0402 [SMD]"]
  R5 = Resistor [tolerance=±5% resistance=47 package="0402 [SMD]"]
  R6 = Resistor [tolerance=±5% resistance=47 package="0402 [SMD]"]
  R7 = Resistor [tolerance=±5% resistance=47 package="0402 [SMD]"]
  R8 = Resistor [tolerance=±5% resistance=47 package="0402 [SMD]"]
  R9 = Resistor [tolerance=±5% resistance=47 package="0402 [SMD]"]
  R10 = Resistor [tolerance=±5% resistance=47 package="0402 [SMD]"]

nets:
  N1: Mod1.GND, LED1.cathode, LED2.cathode, LED3.cathode, LED4.cathode, LED5.cathode, LED6.cathode, LED7.cathode, LED8.cathode, LED9.cathode, LED10.cathode
  N2: Mod1.GPIO14, R10.Pin_1
  N3: Mod1.GPIO18, R9.Pin_1
  N4: Mod1.GPIO23, R8.Pin_1
  N5: Mod1.GPIO24, R7.Pin_1
  N6: Mod1.GPIO25, R6.Pin_1
  N7: Mod1.GPIO8, R5.Pin_1
  N8: Mod1.GPIO12, R4.Pin_1
  N9: Mod1.GPIO16, R3.Pin_1
  N10: Mod1.GPIO20, R2.Pin_1
  N11: Mod1.GPIO21, R1.Pin_1
  N12: LED1.anode, R1.Pin_0
  N13: LED2.anode, R2.Pin_0
  N14: LED3.anode, R3.Pin_0
  N15: LED4.anode, R4.Pin_0
  N16: LED5.anode, R5.Pin_0
  N17: LED6.anode, R6.Pin_0
  N18: LED7.anode, R7.Pin_0
  N19: LED8.anode, R8.Pin_0
  N20: LED9.anode, R9.Pin_0
  N21: LED10.anode, R10.Pin_0
